// Logisim project T8.circ as structural Verilog: 8 circuits, main circuit main
module main (
  input  in_1,
  input  in_2,
  output [7:0] out_3
);

  wire and_1_out, clk_divader_1_out_3, clk_divader_1_out_4, clock_1_out, control_unit_1_out_6,
       control_unit_1_out_7, control_unit_1_out_8, control_unit_1_out_9, control_unit_1_out_10,
       control_unit_1_out_11, control_unit_1_out_12, control_unit_1_out_13, control_unit_1_out_14,
       control_unit_1_out_15, not_1_out;
  wire [7:0] control_unit_1_out_23, program_counter_1_adress_out, rom_1_data;

  CLK_Divader clk_divader_1 (.out_3(clk_divader_1_out_3), .in_1(clock_1_out), .in_2(in_1), .out_4(clk_divader_1_out_4));
  not not_1 (not_1_out, clk_divader_1_out_3);
  and and_1 (and_1_out, in_2, not_1_out);
  Clock clock_1 (.out(clock_1_out));
  Control_Unit control_unit_1 (
    .in_1(out_3), .in_2(clk_divader_1_out_4), .in_3(clock_1_out), .in_4(in_1), .in_5(clk_divader_1_out_3),
    .out_6(control_unit_1_out_6), .out_7(control_unit_1_out_7), .out_8(control_unit_1_out_8),
    .out_9(control_unit_1_out_9), .out_10(control_unit_1_out_10), .out_11(control_unit_1_out_11),
    .out_12(control_unit_1_out_12), .out_13(control_unit_1_out_13), .out_14(control_unit_1_out_14),
    .out_15(control_unit_1_out_15), .out_23(control_unit_1_out_23), .out_26(out_3));  // open: out_16, out_17, out_18, out_19, out_20, out_22, out_24, out_25, out_21
  RAM ram_1 (
    .addr(control_unit_1_out_23), .we(control_unit_1_out_14), .oe(control_unit_1_out_15), .clk(clock_1_out),
    .data(out_3));
  Ram_Adress_Register ram_adress_register_1 (
    .CLK(clock_1_out), .RST(in_1), .ADRESS_OUT(control_unit_1_out_23));  // open: ADRESS_IN, WRT, READ
  LED led_1 (.in(program_counter_1_adress_out[7]));
  Program_Counter program_counter_1 (
    .RST(in_1), .EN(and_1_out), .CLK(clock_1_out), .ADRESS_OUT(program_counter_1_adress_out));  // open: JUMP, ADRESS_IN
  Rx_Register rx_register_1 (
    .DATA_IN(out_3), .WRT(control_unit_1_out_6), .CLK(clock_1_out), .RST(in_1), .READ(control_unit_1_out_7),
    .DATA_OUT(out_3));
  Rx_Register rx_register_2 (
    .DATA_IN(out_3), .WRT(control_unit_1_out_8), .CLK(clock_1_out), .RST(in_1), .READ(control_unit_1_out_9),
    .DATA_OUT(out_3));
  Rx_Register rx_register_3 (
    .DATA_IN(out_3), .WRT(control_unit_1_out_10), .CLK(clock_1_out), .RST(in_1),
    .READ(control_unit_1_out_11), .DATA_OUT(out_3));
  Rx_Register rx_register_4 (
    .DATA_IN(out_3), .WRT(control_unit_1_out_12), .CLK(clock_1_out), .RST(in_1),
    .READ(control_unit_1_out_13), .DATA_OUT(out_3));
  LED led_2 (.in(program_counter_1_adress_out[6]));
  LED led_3 (.in(program_counter_1_adress_out[4]));
  LED led_4 (.in(program_counter_1_adress_out[3]));
  LED led_5 (.in(program_counter_1_adress_out[5]));
  Pull_Resistor pull_resistor_1 (.node(out_3[6]));
  Pull_Resistor pull_resistor_2 (.node(out_3[4]));
  Pull_Resistor pull_resistor_3 (.node(out_3[5]));
  Pull_Resistor pull_resistor_4 (.node(out_3[7]));
  LED led_6 (.in(program_counter_1_adress_out[0]));
  LED led_7 (.in(program_counter_1_adress_out[1]));
  LED led_8 (.in(program_counter_1_adress_out[2]));
  Pull_Resistor pull_resistor_5 (.node(out_3[3]));
  Pull_Resistor pull_resistor_6 (.node(out_3[1]));
  Pull_Resistor pull_resistor_7 (.node(out_3[2]));
  Pull_Resistor pull_resistor_8 (.node(out_3[0]));
  ROM rom_1 (.addr(program_counter_1_adress_out), .data(rom_1_data));
  assign out_3 = and_1_out ? rom_1_data : 8'bz;  // Controlled_Buffer controlled_buffer_1

  // Notes on the sheet:
  //   contents of rom_1 (hex, n*v repeats v):
  //   c1 10
endmodule

module Program_Counter (
  input  RST,
  input  JUMP,
  input  EN,
  input  CLK,
  input  [7:0] ADRESS_IN,
  output [7:0] ADRESS_OUT
);

  wire [7:0] counter_1_q;

  Counter counter_1 (
    .clr(RST), .load(JUMP), .up(1'b1), .count(EN), .clk(CLK), .D(ADRESS_IN), .Q(counter_1_q));  // open: carry
  assign ADRESS_OUT = EN ? counter_1_q : 8'bz;  // Controlled_Buffer controlled_buffer_1
endmodule

module Ram_Adress_Register (
  input  [7:0] ADRESS_IN,
  input  WRT,
  input  CLK,
  input  RST,
  input  READ,
  output [7:0] ADRESS_OUT
);

  wire [7:0] register_1_q;

  Register register_1 (.D(ADRESS_IN), .en(WRT), .clk(CLK), .Q(register_1_q), .clr(RST));
  assign ADRESS_OUT = READ ? register_1_q : 8'bz;  // Controlled_Buffer controlled_buffer_1
endmodule

module Rx_Register (
  input  [7:0] DATA_IN,
  input  WRT,
  input  CLK,
  input  RST,
  input  READ,
  output [7:0] DATA_OUT
);

  wire [7:0] register_1_q;

  Register register_1 (.D(DATA_IN), .en(WRT), .clk(CLK), .Q(register_1_q), .clr(RST));
  assign DATA_OUT = READ ? register_1_q : 8'bz;  // Controlled_Buffer controlled_buffer_1
endmodule

module Instructuon_Register (
  input  [7:0] INST_IN,
  input  WRT,
  input  CLK,
  input  RST,
  input  READ,
  output [15:0] INST_OUT
);

  wire not_1_out;
  wire [7:0] register_1_q, register_2_q;

  Register register_1 (.D(INST_IN), .en(WRT), .clk(CLK), .Q(register_1_q), .clr(RST));
  Register register_2 (.D(register_1_q), .en(WRT), .clk(CLK), .Q(register_2_q), .clr(RST));
  assign INST_OUT = READ ? {register_2_q, register_1_q} : 16'bz;  // Controlled_Buffer controlled_buffer_1
  not not_1 (not_1_out, READ);
  assign INST_OUT = not_1_out ? {16{1'b0}} : 16'bz;  // Controlled_Buffer controlled_buffer_2
endmodule

module CLK_Divader (
  input  in_1,
  input  in_2,
  output out_3,
  output out_4
);

  wire t_ff_1_q;

  T_Flip_Flop t_ff_1 (.T(1'b1), .clk(in_1), .Q(t_ff_1_q), .reset(in_2));  // open: Qn, preset
  T_Flip_Flop t_ff_2 (.T(t_ff_1_q), .clk(in_1), .Q(out_3), .reset(in_2));  // open: Qn, preset
  not not_1 (out_4, out_3);
endmodule

module Control_Unit (
  input  [7:0] in_1,
  input  in_2,
  input  in_3,
  input  in_4,
  input  in_5,
  output out_6,
  output out_7,
  output out_8,
  output out_9,
  output out_10,
  output out_11,
  output out_12,
  output out_13,
  output out_14,
  output out_15,
  output [4:0] out_16,
  output out_17,
  output out_18,
  output out_19,
  output out_20,
  output out_21,
  output out_22,
  output [7:0] out_23,
  output out_24,
  output out_25,
  output [7:0] out_26
);

  wire and_1_out, and_3_out, and_5_out, and_7_out, and_9_out, and_10_out, and_11_out, and_12_out,
       decoder_1_out0, decoder_1_out1, decoder_1_out2, decoder_1_out3, decoder_2_out0, decoder_2_out3;
  wire [1:0] controlled_buffer_3_out, controlled_buffer_4_out, instructuon_register_1_inst_out_2,
       instructuon_register_1_inst_out_3;
  wire [3:0] instructuon_register_1_inst_out;

  Instructuon_Register instructuon_register_1 (
    .INST_IN(in_1), .WRT(in_2), .CLK(in_3), .RST(in_4), .READ(in_5),
    .INST_OUT({instructuon_register_1_inst_out_3[0], instructuon_register_1_inst_out_3[1], instructuon_register_1_inst_out_2[0], instructuon_register_1_inst_out_2[1], out_23, instructuon_register_1_inst_out}));
  Decoder #(.select(2), .enable("false")) decoder_1 (
    .out0(decoder_1_out0), .out1(decoder_1_out1), .out2(decoder_1_out2), .out3(decoder_1_out3),
    .sel(instructuon_register_1_inst_out_2));
  Decoder #(.select(2), .enable("false")) decoder_2 (
    .out0(decoder_2_out0), .out1(out_15), .out2(out_14), .out3(decoder_2_out3),
    .sel(instructuon_register_1_inst_out_3));
  and and_1 (and_1_out, out_15, decoder_1_out0);
  and and_2 (out_7, out_14, decoder_1_out0);
  and and_3 (and_3_out, out_15, decoder_1_out1);
  and and_4 (out_9, out_14, decoder_1_out1);
  and and_5 (and_5_out, out_15, decoder_1_out2);
  and and_6 (out_11, out_14, decoder_1_out2);
  and and_7 (and_7_out, out_15, decoder_1_out3);
  and and_8 (out_13, out_14, decoder_1_out3);
  and and_9 (and_9_out, decoder_1_out0, decoder_2_out3);
  and and_10 (and_10_out, decoder_1_out1, decoder_2_out3);
  and and_11 (and_11_out, decoder_1_out2, decoder_2_out3);
  and and_12 (and_12_out, decoder_1_out3, decoder_2_out3);
  or or_1 (out_6, and_1_out, and_9_out);
  or or_2 (out_8, and_10_out, and_3_out);
  or or_3 (out_10, and_11_out, and_5_out);
  or or_4 (out_12, and_7_out, and_12_out);
  assign out_16 = decoder_2_out0 ? {out_23[5], out_23[6], out_23[7], instructuon_register_1_inst_out_2} : 5'bz;  // Controlled_Buffer controlled_buffer_1
  assign out_26 = decoder_2_out3 ? out_23 : 8'bz;  // Controlled_Buffer controlled_buffer_2
  assign controlled_buffer_3_out = decoder_2_out0 ? {out_23[3], out_23[4]} : 2'bz;  // Controlled_Buffer controlled_buffer_3
  assign controlled_buffer_4_out = decoder_2_out0 ? {out_23[1], out_23[2]} : 2'bz;  // Controlled_Buffer controlled_buffer_4
  Decoder #(.select(2), .enable("false")) decoder_3 (
    .out0(out_17), .out1(out_18), .out2(out_19), .out3(out_20), .sel(controlled_buffer_3_out));
  Decoder #(.select(2), .enable("false")) decoder_4 (
    .out0(out_21), .out1(out_22), .out2(out_24), .out3(out_25), .sel(controlled_buffer_4_out));
endmodule

module Arithmetic_Logic_Unit (
  input  [7:0] in_1,
  input  [7:0] in_2,
  input  in_3,
  input  in_4,
  input  in_5,
  input  in_6
);
endmodule
